# Fritzing sketch Motor test bench (saved by Fritzing 0.9.3b)

parts:
  Componente1 = Arduino Uno (Rev3) - ICSP
  Componente3 = HX711 Module
  Load_Cell1 = Load Cell
  M1 = DC Motor
  Q1 = PHOTOTRANSISTOR REFLECTIVE OBJECT SENSOR [package=qrb1114-side]
  R1 = Resistor [tolerance=±5% resistance=1k package="0603 [SMD]"]
  BREAKOUT1 = ULN2003A module
  MOTOR1 = 28BYJ-48 Stepper Motor
  U1 = LM2596 module

nets:
  N1: Componente1.D10_PWM/SS, Componente3.DO/RX
  N2: Componente1.D11_PWM/MOSI, Componente3.CK/TX
  GND: Componente1.GND, Componente3.GND, M1.pin_1, Q1.C, Q1.K, BREAKOUT1.0V, U1.IN-, U1.OUT-
  N3: Componente1.D3_PWM, Q1.A
  N4: Componente1.D4, BREAKOUT1.In_1
  N5: Componente1.D5_PWM, BREAKOUT1.In_2
  N6: Componente1.D6_PWM, BREAKOUT1.In_3
  N7: Componente1.D7, BREAKOUT1.In_4
  N8: Componente1.IOREF, Componente3.VCC
  N9: Componente1.VIN, R1.Pin_1
  N10: Componente3.E+, Load_Cell1.wire1
  N11: Componente3.E-, Load_Cell1.wire2
  N12: Componente3.A+, Load_Cell1.wire3
  N13: Componente3.A-, Load_Cell1.wire4
  N14: M1.pin_2, U1.IN+
  N15: Q1.E, R1.Pin_0
  N16: BREAKOUT1.+5V, U1.OUT+
  N17: BREAKOUT1.RED_wire, MOTOR1.RED
  N18: BREAKOUT1.ORANGE_wire, MOTOR1.ORANGE
  N19: BREAKOUT1.YELLOW_wire, MOTOR1.YELLOW
  N20: BREAKOUT1.PINK_wire, MOTOR1.PINK
  N21: BREAKOUT1.BLUE_wire, MOTOR1.BLUE

notes:
  12V

custom parts:
  HX711 Module: HX711 is a precision 24-bit analog-to-digital converter (ADC) designed for weigh scales and industrial control applications to interface directly with a bridge sensor.
  Load Cell: A rectangle load cell/weighting pressure Sensor with four wires - Red, white, black, green. Normally corresponding with E+, E-, A+, A- respectively.
  ULN2003A module: ULN2003A 7-way Darlington Transistor Driver on breakoutboard
  LM2596 module: LM2596 DC-DC step down power supply module 3 A.
